# Fritzing sketch esp32-c6-wiring (saved by Fritzing 1.0.8)
breadboards: 1

parts:
  A1 = GY-SHT30 Breakout
  A2 = ESP32-C6-DevKitC-1

nets:
  N1: A1.Pin_1, A2.Pin_1
  N2: A1.Pin_2, A2.Pin_15, A2.Pin_18, A2.Pin_32
  N3: A1.Pin_3, A2.Pin_6
  N4: A1.Pin_4, A2.Pin_5

custom parts:
  ESP32-C6-DevKitC-1: ESP32-C6-DevKitC-1 is an entry-level development board based on ESP32-C6-WROOM-1(U), a general-purpose module with a 8 MB SPI flash. This board integrates complete Wi-Fi, Bluetooth LE, Zigbee, and Thread functions.
